# Fritzing sketch ElbanquosKitchentimer_MK2 (saved by Fritzing 0.9.3b)
circuit board: 12.1005cm x 7.93745cm
breadboards: 5

parts:
  S3 = Pushbutton [package="[THT]"]
  S1 = Pushbutton [package="[THT]"]
  S2 = Pushbutton [package="[THT]"]
  S4 = Pushbutton [package="[THT]"]
  RE1 = Rotary Encoder [package=THT]
  Rotary_Button_Function = Pushbutton [package="[THT]"]
  Spk = Piezo Speaker
  R1 = Resistor [tolerance=±5% resistance=560 package=THT]
  R3 = Resistor [tolerance=±5% resistance=4.7k package=THT]
  Power_Adapter = Power plug
  The_Nano = Arduino Nano (Rev3.0)
  POT1 = Trimmer Potentiometer [maximum_resistance=100kΩ package=THT]
  Q1 = NPN-Transistor [package="TO92 [THT]"]
  C1 = Ceramic Capacitor [capacitance=100nF package="100 mil [THT, multilayer]"]
  button_led_controller = 74HC595 [package="DIP16 [THT]"]
  LED4g = smd LED [color="Green (555nm)" package="1206 [SMD]"]
  LED3g = smd LED [color="Green (555nm)" package="1206 [SMD]"]
  LED1g = smd LED [color="Green (555nm)" package="1206 [SMD]"]
  LED2g = smd LED [color="Green (555nm)" package="1206 [SMD]"]
  7Segment_LED_Controller = MAX7219 [package=dil24]
  7_Segment1 = 7 Segment Display  # not connected
  7_Segment2 = 7 Segment Display  # not connected
  7_Segment3 = 7 Segment Display  # not connected
  7_Segment4 = 7 Segment Display  # not connected
  7_Segment5 = 7 Segment Display  # not connected
  7_Segment6 = 7 Segment Display  # not connected
  7_Segment7 = 7 Segment Display  # not connected
  7_Segment8 = 7 Segment Display  # not connected
  R8 = Resistor [tolerance=±5% resistance=22k package=THT]
  R9 = Resistor [tolerance=±5% resistance=22k package=THT]
  R10 = Resistor [tolerance=±5% resistance=22k package=THT]
  R11 = Resistor [tolerance=±5% resistance=22k package=THT]
  R4 = Resistor [tolerance=±10% resistance=220 package=THT]
  R5 = Resistor [tolerance=±10% resistance=220 package=THT]
  R6 = Resistor [tolerance=±10% resistance=220 package=THT]
  R7 = Resistor [tolerance=±10% resistance=220 package=THT]
  LED1r = LED - 3mm [color="Red (633nm)" package="3 mm [THT]"]
  LED2r = LED - 3mm [color="Red (633nm)" package="3 mm [THT]"]
  LED3r = LED - 3mm [color="Red (633nm)" package="3 mm [THT]"]
  LED4r = LED - 3mm [color="Red (633nm)" package="3 mm [THT]"]
  J3 = Screw terminal - 2 pins [package=THT]

nets:
  VCC: S3.Pin_1, S3.Pin_2, S1.Pin_3, S1.Pin_4, S2.Pin_1, S2.Pin_2, S4.Pin_1, S4.Pin_2, The_Nano.5V, button_led_controller.MR, button_led_controller.VCC, 7Segment_LED_Controller.VCC
  N1: S3.Pin_3, S3.Pin_4, The_Nano.A2, R9.Pin_1
  N2: S1.Pin_1, S1.Pin_2, The_Nano.A4, R11.Pin_1
  N3: S2.Pin_3, S2.Pin_4, The_Nano.A3, R10.Pin_1
  N4: S4.Pin_3, S4.Pin_4, The_Nano.A1, R8.Pin_1
  N5: RE1.EncoderPinA, The_Nano.D11/MOSI
  GND: RE1.EncoderPinC, Rotary_Button_Function.Pin_3, Rotary_Button_Function.Pin_4, Spk.pin1, R1.Pin_1, R3.Pin_1, Power_Adapter.GND, The_Nano.GND, C1.1, button_led_controller.GND, button_led_controller.OE, 7Segment_LED_Controller.GND, R8.Pin_0, R9.Pin_0, R10.Pin_0, R11.Pin_0, J3.pin2
  N6: RE1.EncoderPinB, The_Nano.D10
  N7: Rotary_Button_Function.Pin_1, Rotary_Button_Function.Pin_2, The_Nano.D12/MISO
  N8: Spk.pin2, R3.Pin_0, Q1.E
  N9: R1.Pin_0, POT1.leg2
  VCC_2: Power_Adapter.VCC, The_Nano.VIN, Q1.C, C1.0, J3.pin1
  N10: The_Nano.D2, button_led_controller.SH_CP
  N11: The_Nano.D3, button_led_controller.ST_CP
  N12: The_Nano.D4, button_led_controller.DS
  N13: The_Nano.D5, POT1.leg1
  N14: The_Nano.D6, 7Segment_LED_Controller.DIN
  N15: The_Nano.D7, 7Segment_LED_Controller.CLK
  N16: The_Nano.D8, 7Segment_LED_Controller.LOAD
  N17: POT1.wiper, Q1.B
  N18: button_led_controller.Q1, LED4g.anode, LED4r.cathode
  N19: button_led_controller.Q2, R6.Pin_1
  N20: button_led_controller.Q3, LED3g.anode, LED3r.cathode
  N21: button_led_controller.Q4, R5.Pin_1
  N22: button_led_controller.Q5, LED2g.anode, LED2r.cathode
  N23: button_led_controller.Q6, R4.Pin_1
  N24: button_led_controller.Q7, LED1g.anode, LED1r.cathode
  N25: button_led_controller.Q0, R7.Pin_1
  N26: LED4g.cathode, R7.Pin_0, LED4r.anode
  N27: LED3g.cathode, R6.Pin_0, LED3r.anode
  N28: LED1g.cathode, R4.Pin_0, LED1r.anode
  N29: LED2g.cathode, R5.Pin_0, LED2r.anode
